// Logisim project ULA_FINAL.circ as structural Verilog
module ADD_1 (
  input  A,
  input  B,
  input  VEM_1,
  output S,
  output VAI_1
);

  wire and_1_out, and_2_out, or_1_out, xor_1_out;

  or or_1 (or_1_out, B, VEM_1);
  and and_1 (and_1_out, A, or_1_out);
  and and_2 (and_2_out, B, VEM_1);
  xor xor_1 (xor_1_out, A, B);
  or or_2 (VAI_1, and_1_out, and_2_out);
  xor xor_2 (S, xor_1_out, VEM_1);
endmodule

module ADD_4 (
  input  [3:0] B,
  input  [3:0] A,
  input  VEM,
  output VAI_1,
  output [3:0] out_5
);

  wire add_1_1_vai_1, add_1_3_vai_1, add_1_4_vai_1;

  ADD_1 add_1_1 (.A(A[2]), .B(B[2]), .VEM_1(add_1_3_vai_1), .S(out_5[2]), .VAI_1(add_1_1_vai_1));
  ADD_1 add_1_2 (.A(A[3]), .B(B[3]), .VEM_1(add_1_1_vai_1), .S(out_5[3]), .VAI_1(VAI_1));
  ADD_1 add_1_3 (.A(A[1]), .B(B[1]), .VEM_1(add_1_4_vai_1), .S(out_5[1]), .VAI_1(add_1_3_vai_1));
  ADD_1 add_1_4 (.A(A[0]), .B(B[0]), .VEM_1(VEM), .S(out_5[0]), .VAI_1(add_1_4_vai_1));
endmodule

module SUB_1 (
  input  A,
  input  B,
  input  Vem_1,
  output S,
  output Vai_1
);

  wire A_B_out, and_1_out, and_2_out, not_1_out, or_1_out;

  not not_1 (not_1_out, A);
  or or_1 (or_1_out, B, Vem_1);
  xor A_B (A_B_out, A, B);
  and and_1 (and_1_out, B, Vem_1);
  and and_2 (and_2_out, or_1_out, not_1_out);
  xor A___B_______Vem_1 (S, A_B_out, Vem_1);
  or or_2 (Vai_1, and_1_out, and_2_out);
endmodule

module SUB_4 (
  input  [3:0] B,
  input  [3:0] A,
  input  Vem_1,
  output Vai_1,
  output [3:0] S
);

  wire sub_1_2_vai_1, sub_1_3_vai_1, sub_1_4_vai_1;

  SUB_1 sub_1_1 (.A(A[3]), .B(B[3]), .Vem_1(sub_1_2_vai_1), .S(S[3]), .Vai_1(Vai_1));
  SUB_1 sub_1_2 (.A(A[2]), .B(B[2]), .Vem_1(sub_1_3_vai_1), .S(S[2]), .Vai_1(sub_1_2_vai_1));
  SUB_1 sub_1_3 (.A(A[1]), .B(B[1]), .Vem_1(sub_1_4_vai_1), .S(S[1]), .Vai_1(sub_1_3_vai_1));
  SUB_1 sub_1_4 (.A(A[0]), .B(B[0]), .Vem_1(Vem_1), .S(S[0]), .Vai_1(sub_1_4_vai_1));
endmodule

module Buffer3S (
  input  [3:0] B,
  input  in_2,
  output [3:0] S
);

  assign S[3] = in_2 ? B[3] : 1'bz;  // Controlled_Buffer controlled_buffer_1
  assign S[1] = in_2 ? B[1] : 1'bz;  // Controlled_Buffer controlled_buffer_2
  assign S[2] = in_2 ? B[2] : 1'bz;  // Controlled_Buffer controlled_buffer_3
  assign S[0] = in_2 ? B[0] : 1'bz;  // Controlled_Buffer controlled_buffer_4
endmodule

module BufferI3S (
  input  [3:0] B,
  input  in_2,
  output [3:0] S
);

  assign S[3] = in_2 ? ~B[3] : 1'bz;  // Controlled_Inverter controlled_inverter_1
  assign S[0] = in_2 ? ~B[0] : 1'bz;  // Controlled_Inverter controlled_inverter_2
  assign S[1] = in_2 ? ~B[1] : 1'bz;  // Controlled_Inverter controlled_inverter_3
  assign S[2] = in_2 ? ~B[2] : 1'bz;  // Controlled_Inverter controlled_inverter_4
endmodule

module DCD_3x8 (
  input  [2:0] in_1,
  output S4,
  output S0,
  output S5,
  output S1,
  output S6,
  output S2,
  output S7,
  output S3
);

  wire not_1_out, not_2_out, not_3_out, not_4_out, not_5_out, not_6_out, not_7_out, not_8_out, not_9_out,
       not_10_out, not_11_out, not_12_out;

  not not_1 (not_1_out, in_1[1]);
  and and_1 (S4, in_1[2], not_1_out, not_2_out);
  not not_2 (not_2_out, in_1[0]);
  and and_2 (S5, in_1[2], not_3_out, in_1[0]);
  not not_3 (not_3_out, in_1[1]);
  and and_3 (S6, in_1[2], in_1[1], not_4_out);
  not not_4 (not_4_out, in_1[0]);
  and and_4 (S7, in_1[2], in_1[1], in_1[0]);
  not not_5 (not_5_out, in_1[2]);
  not not_6 (not_6_out, in_1[1]);
  and and_5 (S0, not_5_out, not_6_out, not_7_out);
  not not_7 (not_7_out, in_1[0]);
  not not_8 (not_8_out, in_1[2]);
  and and_6 (S1, not_8_out, not_9_out, in_1[0]);
  not not_9 (not_9_out, in_1[1]);
  not not_10 (not_10_out, in_1[2]);
  and and_7 (S2, not_10_out, in_1[1], not_11_out);
  not not_11 (not_11_out, in_1[0]);
  not not_12 (not_12_out, in_1[2]);
  and and_8 (S3, not_12_out, in_1[1], in_1[0]);
endmodule

module ROT_L (
  input  [3:0] A_B_C_D,
  input  [1:0] X_Y,
  output [3:0] out_3
);

  wire and_1_out, and_2_out, and_3_out, and_4_out, and_5_out, and_6_out, and_7_out, and_8_out, and_9_out;

  and and_1 (and_1_out, ~X_Y[1], ~X_Y[0], A_B_C_D[3]);  // AND_Gate
  and and_2 (and_2_out, ~X_Y[1], X_Y[0], A_B_C_D[2]);  // AND_Gate
  and and_3 (and_3_out, X_Y[1], ~X_Y[0], A_B_C_D[1]);  // AND_Gate
  and and_4 (and_4_out, X_Y[1], X_Y[0], A_B_C_D[0]);
  and and_5 (and_5_out, ~X_Y[1], ~X_Y[0], A_B_C_D[2]);  // AND_Gate
  and and_6 (and_6_out, ~X_Y[1], X_Y[0], A_B_C_D[1]);  // AND_Gate
  and and_7 (and_7_out, X_Y[1], ~X_Y[0], A_B_C_D[0]);  // AND_Gate
  and and_8 (and_8_out, ~X_Y[1], ~X_Y[0], A_B_C_D[1]);  // AND_Gate
  and and_9 (and_9_out, ~X_Y[1], X_Y[0], A_B_C_D[0]);  // AND_Gate
  and and_10 (out_3[3], ~X_Y[1], ~X_Y[0], A_B_C_D[0]);  // AND_Gate
  or or_1 (out_3[0], and_1_out, and_2_out, and_3_out, and_4_out);
  or or_2 (out_3[1], and_5_out, and_6_out, and_7_out);
  or or_3 (out_3[2], and_8_out, and_9_out);
endmodule

module ROT_R (
  input  [3:0] A_B_C_D,
  input  [1:0] X_Y,
  output [3:0] out_3
);

  wire and_1_out, and_2_out, and_3_out, and_4_out, and_5_out, and_6_out, and_7_out, and_8_out, and_9_out;

  and and_1 (and_1_out, ~X_Y[1], ~X_Y[0], A_B_C_D[0]);  // AND_Gate
  and and_2 (and_2_out, ~X_Y[1], X_Y[0], A_B_C_D[1]);  // AND_Gate
  and and_3 (and_3_out, X_Y[1], ~X_Y[0], A_B_C_D[2]);  // AND_Gate
  and and_4 (and_4_out, X_Y[1], X_Y[0], A_B_C_D[3]);
  and and_5 (and_5_out, ~X_Y[1], ~X_Y[0], A_B_C_D[1]);  // AND_Gate
  and and_6 (and_6_out, ~X_Y[1], X_Y[0], A_B_C_D[2]);  // AND_Gate
  and and_7 (and_7_out, X_Y[1], ~X_Y[0], A_B_C_D[3]);  // AND_Gate
  and and_8 (and_8_out, ~X_Y[1], ~X_Y[0], A_B_C_D[2]);  // AND_Gate
  and and_9 (and_9_out, ~X_Y[1], X_Y[0], A_B_C_D[3]);  // AND_Gate
  and and_10 (out_3[3], ~X_Y[1], ~X_Y[0], A_B_C_D[3]);  // AND_Gate
  or or_1 (out_3[0], and_1_out, and_2_out, and_3_out, and_4_out);
  or or_2 (out_3[1], and_5_out, and_6_out, and_7_out);
  or or_3 (out_3[2], and_8_out, and_9_out);
endmodule

module OR_4 (
  input  [3:0] in_1,
  input  [3:0] in_2,
  output [3:0] out_3
);

  or or_1 (out_3[3], in_1[3], in_2[3]);
  or or_2 (out_3[2], in_1[2], in_2[2]);
  or or_3 (out_3[1], in_1[1], in_2[1]);
  or or_4 (out_3[0], in_1[0], in_2[0]);
endmodule

module ULA (
  input  D,
  input  [3:0] A,
  input  [3:0] B,
  input  [2:0] in_4,
  output Overflow,
  output [3:0] out_6
);

  wire add_4_1_vai_1, and_1_out, and_2_out, dcd_3x8_1_s0, dcd_3x8_1_s1, dcd_3x8_1_s2, dcd_3x8_1_s3,
       dcd_3x8_1_s4, dcd_3x8_1_s5, dcd_3x8_1_s6, dcd_3x8_1_s7, not_1_out, sub_4_1_vai_1;
  wire [3:0] add_4_1_out_5, buffer3s_5_s, or_4_1_out_3, rot_l_1_out_3, rot_r_1_out_3, sub_4_1_s;

  or or_1 (Overflow, and_1_out, and_2_out);
  and and_1 (and_1_out, add_4_1_vai_1, dcd_3x8_1_s1);
  and and_2 (and_2_out, sub_4_1_vai_1, dcd_3x8_1_s2);
  DCD_3x8 dcd_3x8_1 (
    .S4(dcd_3x8_1_s4), .S5(dcd_3x8_1_s5), .S6(dcd_3x8_1_s6), .S7(dcd_3x8_1_s7), .S0(dcd_3x8_1_s0),
    .S1(dcd_3x8_1_s1), .S2(dcd_3x8_1_s2), .S3(dcd_3x8_1_s3), .in_1(in_4));
  Buffer3S buffer3s_1 (.B(B), .in_2(dcd_3x8_1_s0), .S(out_6));
  // OR_Gate or_2 has open pins: in0=dcd_3x8_1_s7, in1=dcd_3x8_1_s6, out=open
  ADD_4 add_4_1 (.A(A), .VAI_1(add_4_1_vai_1), .B(B), .VEM(1'b0), .out_5(add_4_1_out_5));
  Buffer3S buffer3s_2 (.B(add_4_1_out_5), .in_2(dcd_3x8_1_s1), .S(out_6));
  SUB_4 sub_4_1 (.A(A), .Vai_1(sub_4_1_vai_1), .B(B), .Vem_1(1'b0), .S(sub_4_1_s));
  Buffer3S buffer3s_3 (.B(sub_4_1_s), .in_2(dcd_3x8_1_s2), .S(out_6));
  OR_4 or_4_1 (.in_1(A), .in_2(B), .out_3(or_4_1_out_3));
  Buffer3S buffer3s_4 (.B(or_4_1_out_3), .in_2(dcd_3x8_1_s3), .S(out_6));
  BufferI3S bufferi3s_1 (.B(B), .in_2(dcd_3x8_1_s4));  // open: S
  not not_1 (not_1_out, D);
  Buffer3S buffer3s_5 (.B(rot_r_1_out_3), .in_2(D), .S(buffer3s_5_s));
  ROT_R rot_r_1 (.out_3(rot_r_1_out_3), .A_B_C_D(A), .X_Y(B[1:0]));
  ROT_L rot_l_1 (.out_3(rot_l_1_out_3), .A_B_C_D(A), .X_Y(B[1:0]));
  Buffer3S buffer3s_6 (.B(rot_l_1_out_3), .in_2(not_1_out), .S(buffer3s_5_s));
  Buffer3S buffer3s_7 (.B(buffer3s_5_s), .in_2(dcd_3x8_1_s5), .S(out_6));
endmodule
